// Logisim project cpu_design.circ as structural Verilog: 1 circuit, main circuit main
module main (
  input  [7:0] in_1,
  input  [7:0] in_2,
  input  in_3
);

  wire clock_1_out;

  Register register_1 (.D(in_2), .en(in_3), .Q(in_1), .clk(clock_1_out));  // open: clr
  Clock clock_1 (.out(clock_1_out));

  // Notes on the sheet:
  //   register a
endmodule
